// Logisim project ALU Circuit Diagram.circ as structural Verilog: 1 circuit, main circuit main
module main (
  input  [2:0] CS2_CS1__CS0,
  input  [3:0] A,
  input  [3:0] B,
  output [3:0] Output,
  output [3:0] out_5,
  output Z,
  output [3:0] out_7,
  output s,
  output V,
  output C,
  output [3:0] out_11
);

  wire adder_1_cout, adder_2_cout, adder_3_cout, and_3_out, and_4_out, and_5_out, not_3_out, Z_out;
  wire [3:0] and_1_out, and_2_out, not_1_out, not_2_out, xnor_1_out, Y_out;

  assign not_1_out = ~{4{CS2_CS1__CS0[1]}};  // NOT_Gate not_1, 4 bits wide
  assign not_2_out = ~B;  // NOT_Gate not_2, 4 bits wide
  assign and_1_out = {4{CS2_CS1__CS0[0]}} & not_1_out & not_1_out & B;  // AND_Gate and_1, 4 bits wide
  assign and_2_out = {4{CS2_CS1__CS0[0]}} & not_2_out & {4{CS2_CS1__CS0[1]}};  // AND_Gate and_2, 4 bits wide
  assign out_11 = A | and_1_out | and_2_out;  // OR_Gate X, 4 bits wide
  not not_3 (not_3_out, CS2_CS1__CS0[0]);
  assign xnor_1_out = ~({4{CS2_CS1__CS0[0]}} ^ {4{CS2_CS1__CS0[1]}});  // XNOR_Gate xnor_1, 4 bits wide
  assign Y_out = xnor_1_out & not_2_out;  // AND_Gate Y, 4 bits wide
  and u_Z (Z_out, not_3_out, CS2_CS1__CS0[2]);
  Adder #(.width(1)) adder_1 (.a(Y_out[0]), .b(out_11[0]), .out(Output[0]), .cin(Z_out), .cout(adder_1_cout));
  and and_3 (and_3_out, adder_1_cout, not_3_out);
  Adder #(.width(1)) adder_2 (.a(Y_out[1]), .b(out_11[1]), .out(Output[1]), .cin(and_3_out), .cout(adder_2_cout));
  Adder #(.width(1)) adder_3 (.a(Y_out[2]), .b(out_11[2]), .out(Output[2]), .cin(and_4_out), .cout(adder_3_cout));
  Adder #(.width(1)) adder_4 (.a(Y_out[3]), .b(out_11[3]), .out(Output[3]), .cin(and_5_out), .cout(C));
  and and_4 (and_4_out, adder_2_cout, not_3_out);
  and and_5 (and_5_out, adder_3_cout, not_3_out);
  xor xor_1 (V, and_5_out, C);
  nor nor_1 (Z, Output[0], Output[1], Output[2], Output[3]);

  assign out_5 = {4{CS2_CS1__CS0[0]}};
  assign out_7 = {4{CS2_CS1__CS0[1]}};
  assign s = Output[3];
endmodule
