// Logisim project FullALU.circ as structural Verilog: 2 circuits, main circuit main
module main (
  input  [2:0] CS2_CS1__CS0,
  input  [3:0] A,
  input  [3:0] B,
  output [3:0] Output,
  output Z,
  output s,
  output V,
  output C
);

  wire adder_1_cout, adder_2_cout, adder_3_cout, adder_4_cout, and_1_out, and_2_out, and_3_out,
       CS1_prime_out, not_1_out, Z_out;
  wire [3:0] B_a_out, B_prime_a_out, B_prime_out, X_out, Y_out;
  wire [3:3] a_out, b_out, xnor_1_out;

  not CS1_prime (CS1_prime_out, CS2_CS1__CS0[1]);
  xnor xnor_1 (xnor_1_out[3], CS2_CS1__CS0[0], CS2_CS1__CS0[1]);
  and u_a (a_out[3], CS2_CS1__CS0[0], CS1_prime_out);
  and u_b (b_out[3], CS2_CS1__CS0[0], CS2_CS1__CS0[1]);
  assign B_prime_out = ~B;  // NOT_Gate B_prime, 4 bits wide
  not not_1 (not_1_out, CS2_CS1__CS0[0]);
  assign B_prime_a_out = {4{b_out[3]}} & B_prime_out;  // AND_Gate B_prime_a, 4 bits wide
  assign B_a_out = {4{a_out[3]}} & B;  // AND_Gate B_a, 4 bits wide
  assign Y_out = {4{xnor_1_out[3]}} & B_prime_out;  // AND_Gate Y, 4 bits wide
  and u_Z (Z_out, not_1_out, CS2_CS1__CS0[2]);
  assign X_out = B_prime_a_out | A | B_a_out;  // OR_Gate X, 4 bits wide
  Adder #(.width(1)) adder_1 (.a(Y_out[0]), .b(X_out[0]), .out(Output[0]), .cin(Z_out), .cout(adder_1_cout));
  and and_1 (and_1_out, adder_1_cout, not_1_out);
  Adder #(.width(1)) adder_2 (.a(Y_out[1]), .b(X_out[1]), .out(Output[1]), .cin(and_1_out), .cout(adder_2_cout));
  Adder #(.width(1)) adder_3 (.a(Y_out[2]), .b(X_out[2]), .out(Output[2]), .cin(and_2_out), .cout(adder_3_cout));
  Adder #(.width(1)) adder_4 (.a(Y_out[3]), .b(X_out[3]), .out(Output[3]), .cin(and_3_out), .cout(adder_4_cout));
  and and_2 (and_2_out, adder_2_cout, not_1_out);
  and and_3 (and_3_out, adder_3_cout, not_1_out);
  and and_4 (C, adder_4_cout, not_1_out);
  xor xor_1 (V, and_3_out, C);
  nor nor_1 (Z, Output[0], Output[1], Output[2], Output[3]);

  assign s = Output[3];
endmodule

module ALU (
  input  [2:0] cs2_cs1_cs0,
  input  [3:0] A,
  input  [3:0] B,
  output C,
  output V,
  output S,
  output Z,
  output [3:0] Output
);

  main ALU (.CS2_CS1__CS0(cs2_cs1_cs0), .B(B), .A(A), .Output(Output), .Z(Z), .s(S), .V(V), .C(C));
endmodule
