// Logisim project floating-point-adder.circ as structural Verilog: 5 circuits, main circuit FPA_BLOCK
module main (
  input  [15:0] A,
  input  [15:0] B,
  output Sign,
  output [10:0] Output__Fraction,
  output [12:0] Un_F,
  output [13:0] F1_With_sign,
  output [13:0] F2__With_sign,
  output [3:0] out_8,
  output out_9,
  output [3:0] Output_Exponent,
  output Overflow_Underflow
);

  wire bitfinder_1_found, not_1_out, subtractor_2_bout;
  wire [3:0] adder_2_out, bitfinder_1_index, exponentdiff_1_abs_a_b, exponentdiff_2_abs_a_b, mx_max_a_b;
  wire [4:4] adder_2_cout, subtractor_2_out;
  wire [12:0] adder_1_out, shifter_1_out, shifter_2_out, shifter_3_out;

  ExponentDiff mx (.A(A[14:11]), .B(B[14:11]), .Max_A_B(mx_max_a_b));  // open: abs_A_B
  ExponentDiff exponentdiff_1 (.A(mx_max_a_b), .B(A[14:11]), .abs_A_B(exponentdiff_1_abs_a_b));  // open: Max_A_B
  Shifter #(.width(13), .shift("lr")) shifter_1 (
    .in({2'b01, A[10:0]}), .\dist (exponentdiff_1_abs_a_b), .out(shifter_1_out));
  ExponentDiff exponentdiff_2 (.A(mx_max_a_b), .B(B[14:11]), .abs_A_B(exponentdiff_2_abs_a_b));  // open: Max_A_B
  fraction_sign_set fraction_sign_set_1 (.F(shifter_1_out), .S(A[15]), .F_prime(F1_With_sign));
  Shifter #(.width(13), .shift("lr")) shifter_2 (
    .in({2'b01, B[10:0]}), .\dist (exponentdiff_2_abs_a_b), .out(shifter_2_out));
  fraction_sign_set fraction_sign_set_2 (.F(shifter_2_out), .S(B[15]), .F_prime(F2__With_sign));
  Adder #(.width(14)) adder_1 (
    .a(F2__With_sign), .b(F1_With_sign), .out({Sign, adder_1_out}), .cin(1'b0), .cout(out_9));
  twos_complement_if_negative twos_complement_if_negative_1 (.in_1({Sign, adder_1_out}), .Output(Un_F));  // open: Sign
  BitFinder #(.width(13), .\type ("high1")) bitfinder_1 (
    .in(Un_F), .index(bitfinder_1_index), .found(bitfinder_1_found));
  not not_1 (not_1_out, bitfinder_1_found);
  Subtractor #(.width(4)) subtractor_1 (.a(4'b1100), .b(bitfinder_1_index), .out(out_8));  // open: bin, bout
  Shifter #(.width(13)) shifter_3 (
    .in(Un_F), .\dist (out_8), .out({shifter_3_out[12], Output__Fraction, shifter_3_out[0]}));
  Adder #(.width(4)) adder_2 (.a(mx_max_a_b), .b(4'b0001), .out(adder_2_out), .cout(adder_2_cout[4]));  // open: cin
  Subtractor #(.width(5)) subtractor_2 (
    .a({adder_2_cout[4], adder_2_out}), .b({1'b0, out_8}), .out({subtractor_2_out[4], Output_Exponent}),
    .bout(subtractor_2_bout));  // open: bin
  or or_1 (Overflow_Underflow, subtractor_2_out[4], not_1_out, subtractor_2_bout);

  // Notes on the sheet:
  //   Sign setting
  //   Addition
  //   Alignment
  //   Normalizing
  //   Truncation
endmodule

module ExponentDiff (
  input  [3:0] A,
  input  [3:0] B,
  output [3:0] abs_A_B,
  output [3:0] Max_A_B
);

  wire subtractor_1_bout;
  wire [3:0] negator_1_out, subtractor_1_out;

  Subtractor #(.width(4)) subtractor_1 (.a(A), .b(B), .out(subtractor_1_out), .bout(subtractor_1_bout));  // open: bin
  Negator #(.width(4)) negator_1 (.in(subtractor_1_out), .out(negator_1_out));
  Multiplexer #(.width(4), .enable("false")) multiplexer_1 (
    .in0(subtractor_1_out), .in1(negator_1_out), .out(abs_A_B), .sel(subtractor_1_bout));
  Multiplexer #(.width(4), .enable("false")) multiplexer_2 (.in0(A), .in1(B), .out(Max_A_B), .sel(subtractor_1_bout));
endmodule

module fraction_sign_set (
  input  [12:0] F,
  input  S,
  output [13:0] F_prime
);

  wire [13:0] bit_extender_1_out, negator_1_out;

  assign bit_extender_1_out = {{1{1'b0}}, F};  // Bit_Extender bit_extender_1
  Negator #(.width(14)) negator_1 (.in(bit_extender_1_out), .out(negator_1_out));
  Multiplexer #(.width(14), .enable("false")) multiplexer_1 (
    .in0(bit_extender_1_out), .in1(negator_1_out), .out(F_prime), .sel(S));
endmodule

module twos_complement_if_negative (
  input  [13:0] in_1,
  output Sign,
  output [12:0] Output
);

  wire [12:0] negator_1_out;

  Negator #(.width(13)) negator_1 (.in(in_1[12:0]), .out(negator_1_out));
  Multiplexer #(.width(13), .enable("false")) multiplexer_1 (
    .in0(in_1[12:0]), .in1(negator_1_out), .out(Output), .sel(in_1[13]));

  assign Sign = in_1[13];
endmodule

module FPA_BLOCK (
  input  [15:0] A,
  input  [15:0] B,
  output [15:0] A_B,
  output Overflow_Underflow
);

  main FPA (
    .A(A), .B(B), .Sign(A_B[15]), .Output__Fraction(A_B[10:0]), .Output_Exponent(A_B[14:11]),
    .Overflow_Underflow(Overflow_Underflow));  // open: Un_F, F1_With_sign, F2__With_sign, out_8, out_9
endmodule
