// Logisim project MIPS.circ as structural Verilog: 6 circuits, main circuit main
module main (
  output out_1,
  output [7:0] out_2,
  output [7:0] out_3,
  output [7:0] Address,
  output [7:0] out_5,
  output [7:0] out_6,
  output out_7,
  output [7:0] zero,
  output [3:0] out_9,
  output [7:0] t0,
  output [7:0] t1,
  output [7:0] t2,
  output [7:0] t3,
  output [7:0] t4,
  output [7:0] sp
);

  wire Clock_out, control_extractor_1_destination_selector, control_extractor_1_immediate_got2_selector,
       control_extractor_1_write_value_selector;
  wire [1:0] PC_MUX_Select_pc_mux_select;
  wire [2:0] control_extractor_1_function;
  wire [3:0] extractor_1_dst_reg, extractor_1_dst_reg2__for_i, extractor_1_opcode, extractor_1_shft_amnt,
       extractor_1_src_reg2, multiplexer_2_out;
  wire [7:0] adder_1_out, adder_2_out, alu_1_output, extractor_1_immediate, extractor_1_target_jump_address,
       multiplexer_1_out, multiplexer_3_out, multiplexer_4_out, ram_1_data;
  wire [11:0] rom_2_data;
  wire [19:0] rom_1_data;

  Register #(.trigger("falling")) PC (.D(multiplexer_1_out), .en(1'b1), .Q(out_5), .clk(Clock_out));  // open: clr
  Adder adder_1 (.a(8'h1), .b(out_5), .out(adder_1_out));  // open: cin, cout
  Multiplexer #(.select(2), .width(8), .enable("false")) multiplexer_1 (
    .in0(adder_1_out), .in1(adder_2_out), .in2(extractor_1_target_jump_address), .out(multiplexer_1_out),
    .sel(PC_MUX_Select_pc_mux_select));  // open: in3
  Adder adder_2 (.a(adder_1_out), .b(extractor_1_immediate), .out(adder_2_out));  // open: cin, cout
  ROM #(.dataWidth(20)) rom_1 (.addr(out_5), .data(rom_1_data));  // open: sel
  PC_MUX_Selector PC_MUX_Select (
    .Datagot1(out_3), .Datagot2(out_6), .Opcode(extractor_1_opcode),
    .PC_MUX_Select(PC_MUX_Select_pc_mux_select));
  Extractor extractor_1 (
    .Instruction(rom_1_data), .Shft_Amnt(extractor_1_shft_amnt), .Dst_Reg(extractor_1_dst_reg),
    .Src_Reg2(extractor_1_src_reg2), .Src_Reg1(out_9), .Opcode(extractor_1_opcode),
    .Immediate(extractor_1_immediate), .dst_reg2__for_I(extractor_1_dst_reg2__for_i),
    .Target_Jump_Address(extractor_1_target_jump_address));
  Clock Clock (.out(Clock_out));
  assign out_2 = {{4{1'b0}}, extractor_1_opcode};  // Bit_Extender bit_extender_1
  Multiplexer #(.width(4), .enable("false")) multiplexer_2 (
    .in0(extractor_1_dst_reg), .in1(extractor_1_dst_reg2__for_i), .out(multiplexer_2_out),
    .sel(control_extractor_1_destination_selector));
  ROM #(.dataWidth(12)) rom_2 (.addr(out_2), .data(rom_2_data), .sel(1'b1));
  Control_Extractor control_extractor_1 (
    .Control(rom_2_data), .Write_Value_Selector(control_extractor_1_write_value_selector),
    .Destination_selector(control_extractor_1_destination_selector), .Memory_Enable(out_1),
    .Immediate_Got2_selector(control_extractor_1_immediate_got2_selector), .R_Enable(out_7),
    .\function (control_extractor_1_function));
  ALU alu_1 (
    .A(out_6), .B(multiplexer_4_out), .ShiftAmount(extractor_1_shft_amnt),
    .\function (control_extractor_1_function), .Output(alu_1_output));  // open: ZeroFlag
  Reg_File reg_file_1 (
    .Value(multiplexer_3_out), .ReadWhich1(out_9), .Enable(out_7), .WriteRegister(multiplexer_2_out),
    .ReadWhich2(extractor_1_src_reg2), .CLK(Clock_out), .DataGot1(out_6), .DataGot2(out_3), .zero(zero),
    .t0(t0), .t1(t1), .t2(t2), .t3(t3), .t4(t4), .sp(sp));
  Multiplexer #(.width(8), .enable("false")) multiplexer_3 (
    .in0(alu_1_output), .in1(ram_1_data), .out(multiplexer_3_out),
    .sel(control_extractor_1_write_value_selector));
  Multiplexer #(.width(8), .enable("false")) multiplexer_4 (
    .in0(out_3), .in1(extractor_1_immediate), .out(multiplexer_4_out),
    .sel(control_extractor_1_immediate_got2_selector));
  Adder adder_3 (.a(out_6), .b(extractor_1_immediate), .out(Address));  // open: cin, cout
  RAM #(.bus("separate")) ram_1 (
    .addr(Address), .din(out_3), .data(ram_1_data), .str(out_1), .sel(1'b1), .clk(Clock_out), .ld(1'b1),
    .clr(1'b0));

  // Notes on the sheet:
  //   Instruction Memory
  //   contents of rom_1 (hex, n*v repeats v):
  //   8020a 26200 807ff e7670 87601 96201 807ff e7670 57601 e2450 5320 26300 807ff e7670 87601 8050f 92203
  //   a203a 51205 d1240 26500 807ff e7670 87601 26400 807ff e7670 87601 96101 807ff e7670 57601 26100
  //   807ff e7670 87601 96201 807ff e7670 57601 1302a 26300 807ff e7670 87601 26700 807ff e7670 87601
  //   71401 64500 11052 e5420 b2150 5420 42200 32114 21102 92206 a202c 64300 62000 26400 807ff e7670 87601
  //   64500 f45fa f45ee 42200 32114 21102 4240
  //   Control ROM
  //   contents of rom_2 (hex, n*v repeats v):
  //   900 b00 40 7a0 5a0 3a0 0 0 1a0 130 d00 700 500 100 300 25*0 11 100 0 0 10 100 22*0 1 100
  //   Data Memory
endmodule

module Reg_File (
  input  [7:0] Value,
  input  [3:0] ReadWhich1,
  input  Enable,
  input  [3:0] WriteRegister,
  input  [3:0] ReadWhich2,
  input  CLK,
  output [7:0] DataGot1,
  output [7:0] DataGot2,
  output [7:0] zero,
  output [7:0] t0,
  output [7:0] t1,
  output [7:0] t2,
  output [7:0] t3,
  output [7:0] t4,
  output [7:0] sp
);

  wire and_1_out, and_2_out, and_3_out, and_4_out, and_5_out, and_6_out, and_7_out, and_8_out,
       decoder_1_out0, decoder_1_out1, decoder_1_out2, decoder_1_out3, decoder_1_out4, decoder_1_out5,
       decoder_1_out6, decoder_1_out7;
  wire [7:0] sp_q, t5_q;

  Decoder #(.select(4), .enable("false")) decoder_1 (
    .out0(decoder_1_out0), .out1(decoder_1_out1), .out2(decoder_1_out2), .out3(decoder_1_out3),
    .out4(decoder_1_out4), .out5(decoder_1_out5), .out6(decoder_1_out6), .out7(decoder_1_out7),
    .sel(WriteRegister));  // open: out8, out9, out10, out11, out12, out13, out14, out15
  and and_1 (and_1_out, decoder_1_out0, Enable);
  and and_2 (and_2_out, decoder_1_out1, Enable);
  and and_3 (and_3_out, decoder_1_out2, Enable);
  and and_4 (and_4_out, decoder_1_out3, Enable);
  and and_5 (and_5_out, decoder_1_out4, Enable);
  and and_6 (and_6_out, decoder_1_out5, Enable);
  and and_7 (and_7_out, decoder_1_out6, Enable);
  and and_8 (and_8_out, decoder_1_out7, Enable);
  Register u_zero (.D({8{1'b0}}), .en(and_1_out), .Q(zero));  // open: clk, clr
  Register u_t0 (.D(Value), .en(and_2_out), .Q(t0), .clk(CLK));  // open: clr
  Register u_t1 (.D(Value), .en(and_3_out), .Q(t1), .clk(CLK));  // open: clr
  Register u_t2 (.D(Value), .en(and_4_out), .Q(t2), .clk(CLK));  // open: clr
  Register u_t3 (.D(Value), .en(and_5_out), .Q(t3), .clk(CLK));  // open: clr
  Register u_t4 (.D(Value), .en(and_6_out), .Q(t4), .clk(CLK));  // open: clr
  Register u_sp (.D(Value), .en(and_7_out), .Q(sp_q), .clk(CLK));  // open: clr
  Register t5 (.D(Value), .en(and_8_out), .Q(t5_q), .clk(CLK));  // open: clr
  Subtractor subtractor_1 (.a({8{1'b1}}), .b(sp_q), .out(sp));  // open: bin, bout
  Multiplexer #(.select(4), .width(8)) multiplexer_1 (
    .in0(zero), .in1(t0), .in2(t1), .in3(t2), .in4(t3), .in5(t4), .in6(sp), .in7(t5_q), .out(DataGot1),
    .sel(ReadWhich1), .en(1'b1));  // open: in8, in9, in10, in11, in12, in13, in14, in15
  Multiplexer #(.select(4), .width(8)) multiplexer_2 (
    .in0(zero), .in1(t0), .in2(t1), .in3(t2), .in4(t3), .in5(t4), .in6(sp), .in7(t5_q), .out(DataGot2),
    .sel(ReadWhich2), .en(1'b1));  // open: in8, in9, in10, in11, in12, in13, in14, in15
endmodule

module Extractor (
  input  [19:0] Instruction,
  output [3:0] Shft_Amnt,
  output [3:0] Dst_Reg,
  output [3:0] Src_Reg2,
  output [3:0] Src_Reg1,
  output [3:0] Opcode,
  output [7:0] Immediate,
  output [3:0] dst_reg2__for_I,
  output [7:0] Target_Jump_Address
);


  assign Dst_Reg = Instruction[7:4];
  assign dst_reg2__for_I = Instruction[11:8];
  assign Immediate = Instruction[7:0];
  assign Opcode = Instruction[19:16];
  assign Shft_Amnt = Instruction[3:0];
  assign Src_Reg1 = Instruction[15:12];
  assign Src_Reg2 = Instruction[11:8];
  assign Target_Jump_Address = Instruction[15:8];
endmodule

module PC_MUX_Selector (
  input  [7:0] Datagot1,
  input  [7:0] Datagot2,
  input  [3:0] Opcode,
  output [1:0] PC_MUX_Select
);

  wire comparator_1_gt, comparator_1_lt;
  wire [0:0] comparator_1_eq, Is_not_equal_out;

  Comparator comparator_1 (
    .a(Datagot1), .b(Datagot2), .gt(comparator_1_gt), .eq(comparator_1_eq[0]), .lt(comparator_1_lt));
  or Is_not_equal (Is_not_equal_out[0], comparator_1_gt, comparator_1_lt);
  Multiplexer #(.select(4), .width(2), .enable("false")) multiplexer_1 (
    .in0(2'b00), .in1(2'b00), .in2(2'b00), .in3(2'b00), .in4(2'b00), .in5(2'b00), .in6(2'b10),
    .in7({1'b0, comparator_1_eq[0]}), .in8(2'b00), .in9(2'b00), .in10(2'b00), .in11(2'b00), .in12(2'b00),
    .in13(2'b00), .in14(2'b00), .in15({1'b0, Is_not_equal_out[0]}), .out(PC_MUX_Select), .sel(Opcode));
endmodule

module Control_Extractor (
  input  [11:0] Control,
  output Write_Value_Selector,
  output Destination_selector,
  output Memory_Enable,
  output Immediate_Got2_selector,
  output R_Enable,
  output [2:0] \function 
);

  wire not_1_out;

  not not_1 (not_1_out, Control[6]);
  and and_1 (R_Enable, not_1_out, Control[8]);

  assign Destination_selector = Control[5];
  assign \function  = Control[11:9];
  assign Immediate_Got2_selector = Control[7];
  assign Memory_Enable = Control[6];
  assign Write_Value_Selector = Control[4];
endmodule

// ALU
module ALU (
  input  [7:0] A,
  input  [7:0] B,
  input  [3:0] ShiftAmount,
  input  [2:0] \function ,
  output [7:0] Output,
  output ZeroFlag
);

  wire [7:0] adder_1_out, and_1_out, nor_1_out, or_1_out, subtractor_1_out;
  wire [15:0] bit_extender_1_out, bit_extender_2_out, shifter_1_out, shifter_2_out;

  assign bit_extender_1_out = {{8{1'b0}}, A};  // Bit_Extender bit_extender_1
  assign bit_extender_2_out = {{8{1'b0}}, A};  // Bit_Extender bit_extender_2
  Adder adder_1 (.a(B), .b(A), .out(adder_1_out));  // open: cin, cout
  Subtractor subtractor_1 (.a(A), .b(B), .out(subtractor_1_out));  // open: bin, bout
  assign and_1_out = A & B;  // AND_Gate and_1, 8 bits wide
  assign or_1_out = A | B;  // OR_Gate or_1, 8 bits wide
  assign nor_1_out = ~(A | B);  // NOR_Gate nor_1, 8 bits wide
  Shifter #(.width(16)) shifter_1 (.in(bit_extender_1_out), .\dist (ShiftAmount), .out(shifter_1_out));
  Shifter #(.width(16), .shift("lr")) shifter_2 (.in(bit_extender_2_out), .\dist (ShiftAmount), .out(shifter_2_out));
  Multiplexer #(.select(3), .width(8), .enable("false")) multiplexer_1 (
    .in0(adder_1_out), .in1(subtractor_1_out), .in2(and_1_out), .in3(or_1_out), .in4(nor_1_out),
    .in5(shifter_1_out[7:0]), .in6(shifter_2_out[7:0]), .in7(A), .out(Output), .sel(\function ));
  nor nor_2 (ZeroFlag, Output[7], Output[6], Output[5], Output[4], Output[3], Output[2], Output[1], Output[0]);
endmodule
