// Logisim project ALU.circ as structural Verilog: 1 circuit, main circuit main
module main (
  input  [7:0] A,
  input  [7:0] B,
  input  [3:0] ShiftAmount,
  input  [2:0] op,
  output [7:0] Function,
  output ZeroFlag
);

  wire [7:0] adder_1_out, and_1_out, nor_1_out, or_1_out, subtractor_1_out;
  wire [15:0] bit_extender_1_out, bit_extender_2_out, shifter_1_out, shifter_2_out;

  assign bit_extender_1_out = {{8{1'b0}}, A};  // Bit_Extender bit_extender_1
  assign bit_extender_2_out = {{8{1'b0}}, A};  // Bit_Extender bit_extender_2
  Adder adder_1 (.a(B), .b(A), .out(adder_1_out));  // open: cin, cout
  Subtractor subtractor_1 (.a(A), .b(B), .out(subtractor_1_out));  // open: bin, bout
  assign and_1_out = A & B;  // AND_Gate and_1, 8 bits wide
  assign or_1_out = A | B;  // OR_Gate or_1, 8 bits wide
  assign nor_1_out = ~(A | B);  // NOR_Gate nor_1, 8 bits wide
  Shifter #(.width(16)) shifter_1 (.in(bit_extender_1_out), .\dist (ShiftAmount), .out(shifter_1_out));
  Shifter #(.width(16), .shift("lr")) shifter_2 (.in(bit_extender_2_out), .\dist (ShiftAmount), .out(shifter_2_out));
  Multiplexer #(.select(3), .width(8), .enable("false")) multiplexer_1 (
    .in0(adder_1_out), .in1(subtractor_1_out), .in2(and_1_out), .in3(or_1_out), .in4(nor_1_out),
    .in5(shifter_1_out[7:0]), .in6(shifter_2_out[7:0]), .out(Function), .sel(op));  // open: in7
  nor nor_2 (ZeroFlag, Function[7], Function[6], Function[5], Function[4], Function[3], Function[2], Function[1], Function[0]);
endmodule
