// Logisim project Merge_ift.circ as structural Verilog: 2 circuits, main circuit main
module main (
  output [7:0] A,
  output [7:0] B,
  output [7:0] out_3,
  output [19:0] out_4,
  output out_5,
  output [7:0] DataGot1,
  output [7:0] DataGot2
);

  wire clock_1_out, decoder_1_out0, decoder_1_out1, decoder_1_out2, decoder_1_out3, decoder_1_out4,
       decoder_1_out5, decoder_1_out6;
  wire [3:0] main_1_dst_reg, main_1_opcode, main_1_shft_amnt, main_1_src_reg1, main_1_src_reg2;
  wire [7:0] adder_1_out, bit_extender_1_out, register_1_q, sp_q, t0_q, t1_q, t2_q, t3_q, t4_q, zero_q;
  wire [11:0] rom_2_data;

  Clock clock_1 (.out(clock_1_out));
  Register #(.trigger("falling")) register_1 (
    .D(adder_1_out), .en(1'b1), .Q(register_1_q), .clk(clock_1_out));  // open: clr
  Adder adder_1 (.a(8'h1), .b(register_1_q), .out(adder_1_out));  // open: cin, cout
  ROM #(.dataWidth(20)) rom_1 (.addr(register_1_q), .data(out_4));  // open: sel
  R_Form_Extractor_main main_1 (
    .Instruction(out_4), .Shft_Amnt(main_1_shft_amnt), .Dst_Reg(main_1_dst_reg), .Src_Reg2(main_1_src_reg2),
    .Src_Reg1(main_1_src_reg1), .Opcode(main_1_opcode));
  assign bit_extender_1_out = {{4{1'b0}}, main_1_opcode};  // Bit_Extender bit_extender_1
  Decoder #(.select(4)) decoder_1 (
    .out0(decoder_1_out0), .out1(decoder_1_out1), .out2(decoder_1_out2), .out3(decoder_1_out3),
    .out4(decoder_1_out4), .out5(decoder_1_out5), .out6(decoder_1_out6), .sel(main_1_dst_reg), .en(out_5));  // open: out7, out8, out9, out10, out11, out12, out13, out14, out15
  ROM #(.dataWidth(12)) rom_2 (
    .addr(bit_extender_1_out), .data({rom_2_data[11:9], out_5, rom_2_data[7:0]}));  // open: sel
  // ALU_main main_2: pin names not known; wires that end beside it: rom_2_data[11:9], out_3, A, B, main_1_shft_amnt
  Register #(.trigger("falling")) zero (.D({8{1'b0}}), .en(decoder_1_out0), .Q(zero_q));  // open: clk, clr
  Register #(.trigger("falling")) t0 (.D(out_3), .en(decoder_1_out1), .Q(t0_q), .clk(clock_1_out));  // open: clr
  Register #(.trigger("falling")) t1 (.D(out_3), .en(decoder_1_out2), .Q(t1_q), .clk(clock_1_out));  // open: clr
  Register #(.trigger("falling")) t2 (.D(out_3), .en(decoder_1_out3), .Q(t2_q), .clk(clock_1_out));  // open: clr
  Register #(.trigger("falling")) t3 (.D(out_3), .en(decoder_1_out4), .Q(t3_q), .clk(clock_1_out));  // open: clr
  Register #(.trigger("falling")) t4 (.D(out_3), .en(decoder_1_out5), .Q(t4_q), .clk(clock_1_out));  // open: clr
  Register #(.trigger("falling")) sp (.D(out_3), .en(decoder_1_out6), .Q(sp_q), .clk(clock_1_out));  // open: clr
  Multiplexer #(.select(4), .width(8)) multiplexer_1 (
    .in0(zero_q), .in1(t0_q), .in2(t1_q), .in3(t2_q), .in4(t3_q), .in5(t4_q), .in6(sp_q), .in7(8'h1),
    .out(A), .sel(main_1_src_reg2), .en(1'b1));  // open: in8, in9, in10, in11, in12, in13, in14, in15
  Multiplexer #(.select(4), .width(8)) multiplexer_2 (
    .in0(zero_q), .in1(t0_q), .in2(t1_q), .in3(t2_q), .in4(t3_q), .in5(t4_q), .in6(sp_q), .in7(8'h1),
    .out(B), .sel(main_1_src_reg1), .en(1'b1));  // open: in8, in9, in10, in11, in12, in13, in14, in15

  assign DataGot1 = A;
  assign DataGot2 = B;

  // Notes on the sheet:
  //   contents of rom_1 (hex, n*v repeats v):
  //   d3720 d2240 e2200 d4740 b4250
  //   contents of rom_2 (hex, n*v repeats v):
  //   900 b00 8*0 d00 700 500 100 300 25*0 11 100 0 0 10 100 22*0 1 100
endmodule

module Reg_File (
  input  [7:0] Value,
  input  [3:0] ReadWhich1,
  input  Enable,
  input  [3:0] WriteRegister,
  input  [3:0] ReadWhich2,
  output [7:0] DataGot1,
  output [7:0] DataGot2
);

  wire clock_1_out, decoder_1_out0, decoder_1_out1, decoder_1_out2, decoder_1_out3, decoder_1_out4,
       decoder_1_out5, decoder_1_out6;
  wire [7:0] sp_q, t0_q, t1_q, t2_q, t3_q, t4_q, zero_q;

  Clock clock_1 (.out(clock_1_out));
  Decoder #(.select(4)) decoder_1 (
    .out0(decoder_1_out0), .out1(decoder_1_out1), .out2(decoder_1_out2), .out3(decoder_1_out3),
    .out4(decoder_1_out4), .out5(decoder_1_out5), .out6(decoder_1_out6), .sel(WriteRegister), .en(Enable));  // open: out7, out8, out9, out10, out11, out12, out13, out14, out15
  Register #(.trigger("falling")) zero (.D({8{1'b0}}), .en(decoder_1_out0), .Q(zero_q));  // open: clk, clr
  Register #(.trigger("falling")) t0 (.D(Value), .en(decoder_1_out1), .Q(t0_q), .clk(clock_1_out));  // open: clr
  Register #(.trigger("falling")) t1 (.D(Value), .en(decoder_1_out2), .Q(t1_q), .clk(clock_1_out));  // open: clr
  Register #(.trigger("falling")) t2 (.D(Value), .en(decoder_1_out3), .Q(t2_q), .clk(clock_1_out));  // open: clr
  Register #(.trigger("falling")) t3 (.D(Value), .en(decoder_1_out4), .Q(t3_q), .clk(clock_1_out));  // open: clr
  Register #(.trigger("falling")) t4 (.D(Value), .en(decoder_1_out5), .Q(t4_q), .clk(clock_1_out));  // open: clr
  Register #(.trigger("falling")) sp (.D(Value), .en(decoder_1_out6), .Q(sp_q), .clk(clock_1_out));  // open: clr
  Multiplexer #(.select(4), .width(8)) multiplexer_1 (
    .in0(zero_q), .in1(t0_q), .in2(t1_q), .in3(t2_q), .in4(t3_q), .in5(t4_q), .in6(sp_q), .in7(8'h1),
    .out(DataGot1), .sel(ReadWhich1), .en(1'b1));  // open: in8, in9, in10, in11, in12, in13, in14, in15
  Multiplexer #(.select(4), .width(8)) multiplexer_2 (
    .in0(zero_q), .in1(t0_q), .in2(t1_q), .in3(t2_q), .in4(t3_q), .in5(t4_q), .in6(sp_q), .in7(8'h1),
    .out(DataGot2), .sel(ReadWhich2), .en(1'b1));  // open: in8, in9, in10, in11, in12, in13, in14, in15
endmodule
