// Logisim project R_Form_Extractor.circ as structural Verilog: 1 circuit, main circuit main
// R_Form_Extractor
module main (
  input  [19:0] Instruction,
  output [3:0] Shft_Amnt,
  output [3:0] Dst_Reg,
  output [3:0] Src_Reg2,
  output [3:0] Src_Reg1,
  output [3:0] Opcode
);


  assign Dst_Reg = Instruction[7:4];
  assign Opcode = Instruction[19:16];
  assign Shft_Amnt = Instruction[3:0];
  assign Src_Reg1 = Instruction[15:12];
  assign Src_Reg2 = Instruction[11:8];
endmodule
