// Logisim project Rfile.circ as structural Verilog: 1 circuit, main circuit main
// R_File
module main (
  input  [7:0] Value,
  input  [3:0] ReadWhich1,
  input  Enable,
  input  [3:0] WriteRegister,
  input  [3:0] ReadWhich2,
  output [7:0] DataGot1,
  output [7:0] DataGot2
);

  wire button_1_out, decoder_1_out0, decoder_1_out1, decoder_1_out2, decoder_1_out3, decoder_1_out4,
       decoder_1_out5, decoder_1_out6;
  wire [7:0] sp_q, t0_q, t1_q, t2_q, t3_q, t4_q, zero_q;

  Button button_1 (.out(button_1_out));
  Decoder #(.select(4)) decoder_1 (
    .out0(decoder_1_out0), .out1(decoder_1_out1), .out2(decoder_1_out2), .out3(decoder_1_out3),
    .out4(decoder_1_out4), .out5(decoder_1_out5), .out6(decoder_1_out6), .sel(WriteRegister), .en(Enable));  // open: out7, out8, out9, out10, out11, out12, out13, out14, out15
  Register #(.trigger("falling")) zero (.D({8{1'b0}}), .en(decoder_1_out0), .Q(zero_q));  // open: clk, clr
  Register #(.trigger("falling")) t0 (.D(Value), .en(decoder_1_out1), .Q(t0_q), .clk(button_1_out));  // open: clr
  Register #(.trigger("falling")) t1 (.D(Value), .en(decoder_1_out2), .Q(t1_q), .clk(button_1_out));  // open: clr
  Register #(.trigger("falling")) t2 (.D(Value), .en(decoder_1_out3), .Q(t2_q), .clk(button_1_out));  // open: clr
  Register #(.trigger("falling")) t3 (.D(Value), .en(decoder_1_out4), .Q(t3_q), .clk(button_1_out));  // open: clr
  Register #(.trigger("falling")) t4 (.D(Value), .en(decoder_1_out5), .Q(t4_q), .clk(button_1_out));  // open: clr
  Register #(.trigger("falling")) sp (.D(Value), .en(decoder_1_out6), .Q(sp_q), .clk(button_1_out));  // open: clr
  Multiplexer #(.select(4), .width(8)) multiplexer_1 (
    .in0(zero_q), .in1(t0_q), .in2(t1_q), .in3(t2_q), .in4(t3_q), .in5(t4_q), .in6(sp_q), .in7(8'h1),
    .out(DataGot1), .sel(ReadWhich1), .en(1'b1));  // open: in8, in9, in10, in11, in12, in13, in14, in15
  Multiplexer #(.select(4), .width(8)) multiplexer_2 (
    .in0(zero_q), .in1(t0_q), .in2(t1_q), .in3(t2_q), .in4(t3_q), .in5(t4_q), .in6(sp_q), .in7(8'h1),
    .out(DataGot2), .sel(ReadWhich2), .en(1'b1));  // open: in8, in9, in10, in11, in12, in13, in14, in15
endmodule
