// Logisim project pipelined.circ as structural Verilog: 11 circuits, main circuit main
module main (
  output [1:0] ForwardB,
  output [1:0] ForwardA,
  output [7:0] out_3,
  output [7:0] out_4,
  output [2:0] out_5,
  output [7:0] out_6,
  output [3:0] out_7,
  output [7:0] ALU_OUTPUT,
  output out_9,
  output [7:0] EX_MEM_OUTPUT,
  output [7:0] MEM_WB_OUTPUT,
  output [3:0] MEM_WB_Dest_REG,
  output [7:0] zero,
  output [7:0] t0,
  output [7:0] t1,
  output [7:0] t2,
  output [7:0] t3,
  output [7:0] t4
);

  wire Clock_out, control_extractor_1_r_enable, control_extractor_1_write_value_selector, ex_mem_1_dest_2,
       ex_mem_1_r_val, id_ex_1_r_val, id_ex_1_wr, not_1_out, not_2_out;
  wire [2:0] control_extractor_1_function;
  wire [3:0] ex_mem_1_dest_reg, Extractor_dst_reg, Extractor_shft_amnt, Extractor_src_reg1,
       Extractor_src_reg2, id_ex_1_dest_reg_2, id_ex_1_src1_2, id_ex_1_src2_2, if_id_1_dest, if_id_1_opcode,
       if_id_1_src1, if_id_1_src2;
  wire [7:0] adder_1_out, bit_extender_1_out, id_ex_1_d1_2, id_ex_1_d2_2, reg_file_1_datagot1,
       reg_file_1_datagot2;
  wire [11:0] rom_2_data;
  wire [19:0] rom_1_data;

  Clock Clock (.out(Clock_out));
  Register PC (.D(adder_1_out), .en(1'b1), .Q(out_6), .clk(not_1_out));  // open: clr
  not not_1 (not_1_out, Clock_out);
  Adder adder_1 (.a(8'h1), .b(out_6), .out(adder_1_out));  // open: cin, cout
  ROM #(.dataWidth(20)) rom_1 (.addr(out_6), .data(rom_1_data));  // open: sel
  Extractor Extractor (
    .Instruction(rom_1_data), .Shft_Amnt(Extractor_shft_amnt), .Dst_Reg(Extractor_dst_reg),
    .Src_Reg2(Extractor_src_reg2), .Src_Reg1(Extractor_src_reg1), .Opcode(out_7));  // open: Immediate, dst_reg2__for_I, Target_Jump_Address
  IF_ID if_id_1 (
    .in_1(Extractor_shft_amnt), .in_2(Extractor_dst_reg), .in_3(Extractor_src_reg2),
    .in_4(Extractor_src_reg1), .in_5(out_7), .in_6(not_1_out), .DEST(if_id_1_dest), .SRC1(if_id_1_src1),
    .SRC2(if_id_1_src2), .OPCODE(if_id_1_opcode));  // open: shift
  not not_2 (not_2_out, not_1_out);
  assign bit_extender_1_out = {{4{1'b0}}, if_id_1_opcode};  // Bit_Extender bit_extender_1
  Reg_File reg_file_1 (
    .Value(MEM_WB_OUTPUT), .ReadWhich1(if_id_1_src1), .Enable(out_9), .WriteRegister(MEM_WB_Dest_REG),
    .ReadWhich2(if_id_1_src2), .CLK(not_2_out), .DataGot1(reg_file_1_datagot1),
    .DataGot2(reg_file_1_datagot2), .zero(zero), .t0(t0), .t1(t1), .t2(t2), .t3(t3), .t4(t4));  // open: sp
  ROM #(.dataWidth(12)) rom_2 (.addr(bit_extender_1_out), .data(rom_2_data));  // open: sel
  Control_Extractor control_extractor_1 (
    .Control(rom_2_data), .Write_Value_Selector(control_extractor_1_write_value_selector),
    .R_Enable(control_extractor_1_r_enable), .\function (control_extractor_1_function));  // open: Destination_selector
  ID_EX id_ex_1 (
    .clk(not_1_out), .src1(if_id_1_src1), .src2(if_id_1_src2), .D1(reg_file_1_datagot1),
    .D2(reg_file_1_datagot2), .wb(control_extractor_1_write_value_selector),
    .rval(control_extractor_1_r_enable), .func(control_extractor_1_function), .dest_reg(if_id_1_dest),
    .src1_2(id_ex_1_src1_2), .src2_2(id_ex_1_src2_2), .D1_2(id_ex_1_d1_2), .D2_2(id_ex_1_d2_2),
    .WR(id_ex_1_wr), .R_val(id_ex_1_r_val), .func_2(out_5), .dest_reg_2(id_ex_1_dest_reg_2));  // open: dest, out_16
  EX_MEM ex_mem_1 (
    .clk(not_1_out), .src1(id_ex_1_src1_2), .src2(id_ex_1_src2_2), .des_reg(id_ex_1_dest_reg_2),
    .\output (ALU_OUTPUT), .wb(id_ex_1_wr), .rval(id_ex_1_r_val), .func(out_5), .dest_reg(ex_mem_1_dest_reg),
    .output_2(EX_MEM_OUTPUT), .dest_2(ex_mem_1_dest_2), .R_val(ex_mem_1_r_val));  // open: dest, src1_2, src2_2, WR, func_2
  Sub_Forwarding_Unit F_Unit_1 (
    .EX_MEM_SourceRegister(id_ex_1_src1_2), .EX_MEM_WriteRegister(ex_mem_1_dest_reg),
    .MEM_WB_WriteRegister(MEM_WB_Dest_REG), .Selector(ForwardB));
  Sub_Forwarding_Unit F__Unit_2 (
    .EX_MEM_SourceRegister(id_ex_1_src2_2), .EX_MEM_WriteRegister(ex_mem_1_dest_reg),
    .MEM_WB_WriteRegister(MEM_WB_Dest_REG), .Selector(ForwardA));
  MEM_WB mem_wb_1 (
    .clk(not_1_out), .des_reg(ex_mem_1_dest_reg), .\output (EX_MEM_OUTPUT), .dest(ex_mem_1_dest_2),
    .rval(ex_mem_1_r_val), .dest_reg(MEM_WB_Dest_REG), .output_2(MEM_WB_OUTPUT), .R_val(out_9));  // open: src1, src2, wb, func, src1_2, src2_2, WR, dest_2, func_2
  Multiplexer #(.select(2), .width(8), .enable("false")) multiplexer_1 (
    .in0(id_ex_1_d1_2), .in1(EX_MEM_OUTPUT), .in2(MEM_WB_OUTPUT), .out(out_4), .sel(ForwardB));  // open: in3
  Multiplexer #(.select(2), .width(8), .enable("false")) multiplexer_2 (
    .in0(id_ex_1_d2_2), .in1(EX_MEM_OUTPUT), .in2(MEM_WB_OUTPUT), .out(out_3), .sel(ForwardA));  // open: in3
  ALU alu_1 (.A(out_3), .B(out_4), .\function (out_5), .Output(ALU_OUTPUT));  // open: ShiftAmount, ZeroFlag

  // Notes on the sheet:
  //   Instruction Memory
  //   contents of rom_1 (hex, n*v repeats v):
  //   d3420 e2350 b2450 d5450 c5450 e5330 b4440 d3430
  //   Control ROM
  //   contents of rom_2 (hex, n*v repeats v):
  //   900 b00 40 7a0 5a0 3a0 0 0 1a0 130 d00 700 500 100 300 25*0 11 100 0 0 10 100 22*0 1 100
  //   Forwarding
endmodule

module Reg_File (
  input  [7:0] Value,
  input  [3:0] ReadWhich1,
  input  Enable,
  input  [3:0] WriteRegister,
  input  [3:0] ReadWhich2,
  input  CLK,
  output [7:0] DataGot1,
  output [7:0] DataGot2,
  output [7:0] zero,
  output [7:0] t0,
  output [7:0] t1,
  output [7:0] t2,
  output [7:0] t3,
  output [7:0] t4,
  output [7:0] sp
);

  wire and_1_out, and_2_out, and_3_out, and_4_out, and_5_out, and_6_out, and_7_out, and_8_out,
       decoder_1_out0, decoder_1_out1, decoder_1_out2, decoder_1_out3, decoder_1_out4, decoder_1_out5,
       decoder_1_out6, decoder_1_out7;
  wire [7:0] sp_q, t5_q;

  Decoder #(.select(4), .enable("false")) decoder_1 (
    .out0(decoder_1_out0), .out1(decoder_1_out1), .out2(decoder_1_out2), .out3(decoder_1_out3),
    .out4(decoder_1_out4), .out5(decoder_1_out5), .out6(decoder_1_out6), .out7(decoder_1_out7),
    .sel(WriteRegister));  // open: out8, out9, out10, out11, out12, out13, out14, out15
  and and_1 (and_1_out, decoder_1_out0, Enable);
  and and_2 (and_2_out, decoder_1_out1, Enable);
  and and_3 (and_3_out, decoder_1_out2, Enable);
  and and_4 (and_4_out, decoder_1_out3, Enable);
  and and_5 (and_5_out, decoder_1_out4, Enable);
  and and_6 (and_6_out, decoder_1_out5, Enable);
  and and_7 (and_7_out, decoder_1_out6, Enable);
  and and_8 (and_8_out, decoder_1_out7, Enable);
  Register u_zero (.D({8{1'b0}}), .en(and_1_out), .Q(zero));  // open: clk, clr
  Register u_t0 (.D(Value), .en(and_2_out), .Q(t0), .clk(CLK));  // open: clr
  Register u_t1 (.D(Value), .en(and_3_out), .Q(t1), .clk(CLK));  // open: clr
  Register u_t2 (.D(Value), .en(and_4_out), .Q(t2), .clk(CLK));  // open: clr
  Register u_t3 (.D(Value), .en(and_5_out), .Q(t3), .clk(CLK));  // open: clr
  Register u_t4 (.D(Value), .en(and_6_out), .Q(t4), .clk(CLK));  // open: clr
  Register u_sp (.D(Value), .en(and_7_out), .Q(sp_q), .clk(CLK));  // open: clr
  Register t5 (.D(Value), .en(and_8_out), .Q(t5_q), .clk(CLK));  // open: clr
  Subtractor subtractor_1 (.a({8{1'b1}}), .b(sp_q), .out(sp));  // open: bin, bout
  Multiplexer #(.select(4), .width(8)) multiplexer_1 (
    .in0(zero), .in1(t0), .in2(t1), .in3(t2), .in4(t3), .in5(t4), .in6(sp), .in7(t5_q), .out(DataGot1),
    .sel(ReadWhich1), .en(1'b1));  // open: in8, in9, in10, in11, in12, in13, in14, in15
  Multiplexer #(.select(4), .width(8)) multiplexer_2 (
    .in0(zero), .in1(t0), .in2(t1), .in3(t2), .in4(t3), .in5(t4), .in6(sp), .in7(t5_q), .out(DataGot2),
    .sel(ReadWhich2), .en(1'b1));  // open: in8, in9, in10, in11, in12, in13, in14, in15
endmodule

module Extractor (
  input  [19:0] Instruction,
  output [3:0] Shft_Amnt,
  output [3:0] Dst_Reg,
  output [3:0] Src_Reg2,
  output [3:0] Src_Reg1,
  output [3:0] Opcode,
  output [7:0] Immediate,
  output [3:0] dst_reg2__for_I,
  output [7:0] Target_Jump_Address
);


  assign Dst_Reg = Instruction[7:4];
  assign dst_reg2__for_I = Instruction[11:8];
  assign Immediate = Instruction[7:0];
  assign Opcode = Instruction[19:16];
  assign Shft_Amnt = Instruction[3:0];
  assign Src_Reg1 = Instruction[15:12];
  assign Src_Reg2 = Instruction[11:8];
  assign Target_Jump_Address = Instruction[15:8];
endmodule

module PC_MUX_Selector (
  input  [7:0] Datagot1,
  input  [7:0] Datagot2,
  input  [3:0] Opcode,
  output [1:0] PC_MUX_Select
);

  wire comparator_1_gt, comparator_1_lt;
  wire [0:0] comparator_1_eq, Is_not_equal_out;

  Comparator comparator_1 (
    .a(Datagot1), .b(Datagot2), .gt(comparator_1_gt), .eq(comparator_1_eq[0]), .lt(comparator_1_lt));
  or Is_not_equal (Is_not_equal_out[0], comparator_1_gt, comparator_1_lt);
  Multiplexer #(.select(4), .width(2), .enable("false")) multiplexer_1 (
    .in0(2'b00), .in1(2'b00), .in2(2'b00), .in3(2'b00), .in4(2'b00), .in5(2'b00), .in6(2'b10),
    .in7({1'b0, comparator_1_eq[0]}), .in8(2'b00), .in9(2'b00), .in10(2'b00), .in11(2'b00), .in12(2'b00),
    .in13(2'b00), .in14(2'b00), .in15({1'b0, Is_not_equal_out[0]}), .out(PC_MUX_Select), .sel(Opcode));
endmodule

module Control_Extractor (
  input  [11:0] Control,
  output Write_Value_Selector,
  output Destination_selector,
  output R_Enable,
  output [2:0] \function 
);


  assign Destination_selector = Control[5];
  assign \function  = Control[11:9];
  assign R_Enable = Control[8];
  assign Write_Value_Selector = Control[4];
endmodule

// ALU
module ALU (
  input  [7:0] A,
  input  [7:0] B,
  input  [3:0] ShiftAmount,
  input  [2:0] \function ,
  output [7:0] Output,
  output ZeroFlag
);

  wire [7:0] adder_1_out, and_1_out, nor_1_out, or_1_out, subtractor_1_out;
  wire [15:0] bit_extender_1_out, bit_extender_2_out, shifter_1_out, shifter_2_out;

  assign bit_extender_1_out = {{8{1'b0}}, A};  // Bit_Extender bit_extender_1
  assign bit_extender_2_out = {{8{1'b0}}, A};  // Bit_Extender bit_extender_2
  Adder adder_1 (.a(B), .b(A), .out(adder_1_out));  // open: cin, cout
  Subtractor subtractor_1 (.a(A), .b(B), .out(subtractor_1_out));  // open: bin, bout
  assign and_1_out = A & B;  // AND_Gate and_1, 8 bits wide
  assign or_1_out = A | B;  // OR_Gate or_1, 8 bits wide
  assign nor_1_out = ~(A | B);  // NOR_Gate nor_1, 8 bits wide
  Shifter #(.width(16)) shifter_1 (.in(bit_extender_1_out), .\dist (ShiftAmount), .out(shifter_1_out));
  Shifter #(.width(16), .shift("lr")) shifter_2 (.in(bit_extender_2_out), .\dist (ShiftAmount), .out(shifter_2_out));
  Multiplexer #(.select(3), .width(8), .enable("false")) multiplexer_1 (
    .in0(adder_1_out), .in1(subtractor_1_out), .in2(and_1_out), .in3(or_1_out), .in4(nor_1_out),
    .in5(shifter_1_out[7:0]), .in6(shifter_2_out[7:0]), .in7(A), .out(Output), .sel(\function ));
  nor nor_2 (ZeroFlag, Output[7], Output[6], Output[5], Output[4], Output[3], Output[2], Output[1], Output[0]);
endmodule

module IF_ID (
  input  [3:0] in_1,
  input  [3:0] in_2,
  input  [3:0] in_3,
  input  [3:0] in_4,
  input  [3:0] in_5,
  input  in_6,
  output [3:0] shift,
  output [3:0] DEST,
  output [3:0] SRC1,
  output [3:0] SRC2,
  output [3:0] OPCODE
);

  Register #(.width(4)) register_1 (.D(in_1), .Q(shift), .clk(in_6));  // open: en, clr
  Register #(.width(4)) register_2 (.D(in_2), .Q(DEST), .clk(in_6));  // open: en, clr
  Register #(.width(4)) register_3 (.D(in_3), .Q(SRC1), .clk(in_6));  // open: en, clr
  Register #(.width(4)) register_4 (.D(in_4), .Q(SRC2), .clk(in_6));  // open: en, clr
  Register #(.width(4)) register_5 (.D(in_5), .Q(OPCODE), .clk(in_6));  // open: en, clr
endmodule

module ID_EX (
  input  clk,
  input  [3:0] src1,
  input  [3:0] src2,
  input  [7:0] D1,
  input  [7:0] D2,
  input  wb,
  input  dest,
  input  rval,
  input  [2:0] func,
  input  [3:0] dest_reg,
  output [3:0] src1_2,
  output [3:0] src2_2,
  output [7:0] D1_2,
  output [7:0] D2_2,
  output WR,
  output out_16,
  output R_val,
  output [2:0] func_2,
  output [3:0] dest_reg_2
);

  Register #(.width(4)) register_1 (.D(src1), .Q(src1_2), .clk(clk));  // open: en, clr
  Register #(.width(4)) register_2 (.D(src2), .Q(src2_2), .clk(clk));  // open: en, clr
  Register register_3 (.D(D1), .Q(D1_2), .clk(clk));  // open: en, clr
  Register register_4 (.D(D2), .Q(D2_2), .clk(clk));  // open: en, clr
  Register #(.width(1)) register_5 (.D(wb), .Q(WR), .clk(clk));  // open: en, clr
  Register #(.width(1)) register_6 (.D(dest), .Q(out_16), .clk(clk));  // open: en, clr
  Register #(.width(1)) register_7 (.D(rval), .Q(R_val), .clk(clk));  // open: en, clr
  Register #(.width(3)) register_8 (.D(func), .Q(func_2), .clk(clk));  // open: en, clr
  Register #(.width(4)) register_9 (.D(dest_reg), .Q(dest_reg_2), .clk(clk));  // open: en, clr
endmodule

module EX_MEM (
  input  clk,
  input  [3:0] src1,
  input  [3:0] src2,
  input  [3:0] des_reg,
  input  [7:0] \output ,
  input  wb,
  input  dest,
  input  rval,
  input  [2:0] func,
  output [3:0] src1_2,
  output [3:0] src2_2,
  output [3:0] dest_reg,
  output [7:0] output_2,
  output WR,
  output dest_2,
  output R_val,
  output [2:0] func_2
);

  Register #(.width(4)) register_1 (.D(src1), .Q(src1_2), .clk(clk));  // open: en, clr
  Register register_2 (.D(\output ), .Q(output_2), .clk(clk));  // open: en, clr
  Register #(.width(1)) register_3 (.D(wb), .Q(WR), .clk(clk));  // open: en, clr
  Register #(.width(1)) register_4 (.D(dest), .Q(dest_2), .clk(clk));  // open: en, clr
  Register #(.width(1)) register_5 (.D(rval), .Q(R_val), .clk(clk));  // open: en, clr
  Register #(.width(3)) register_6 (.D(func), .Q(func_2), .clk(clk));  // open: en, clr
  Register #(.width(4)) register_7 (.D(src2), .Q(src2_2), .clk(clk));  // open: en, clr
  Register #(.width(4)) register_8 (.D(des_reg), .Q(dest_reg), .clk(clk));  // open: en, clr
endmodule

module Sub_Forwarding_Unit (
  input  [3:0] EX_MEM_SourceRegister,
  input  [3:0] EX_MEM_WriteRegister,
  input  [3:0] MEM_WB_WriteRegister,
  output [1:0] Selector
);

  wire not_1_out, not_2_out, not_3_out, or_1_out, or_2_out, or_3_out, or_4_out;
  wire [3:0] xor_1_out, xor_2_out;

  assign xor_1_out = EX_MEM_SourceRegister ^ EX_MEM_WriteRegister;  // XOR_Gate xor_1, 4 bits wide
  assign xor_2_out = EX_MEM_SourceRegister ^ MEM_WB_WriteRegister;  // XOR_Gate xor_2, 4 bits wide
  or or_1 (or_1_out, EX_MEM_SourceRegister[0], EX_MEM_SourceRegister[1], EX_MEM_SourceRegister[2], EX_MEM_SourceRegister[3]);
  not not_1 (not_1_out, or_2_out);
  or or_2 (or_2_out, xor_1_out[0], xor_1_out[1], xor_1_out[2], xor_1_out[3]);
  or or_3 (or_3_out, EX_MEM_SourceRegister[0], EX_MEM_SourceRegister[1], EX_MEM_SourceRegister[2], EX_MEM_SourceRegister[3]);
  or or_4 (or_4_out, xor_2_out[0], xor_2_out[1], xor_2_out[2], xor_2_out[3]);
  not not_2 (not_2_out, or_4_out);
  and and_1 (Selector[0], or_1_out, not_1_out);
  not not_3 (not_3_out, Selector[0]);
  and and_2 (Selector[1], or_3_out, not_3_out, not_2_out);
endmodule

module MEM_WB (
  input  clk,
  input  [3:0] src1,
  input  [3:0] src2,
  input  [3:0] des_reg,
  input  [7:0] \output ,
  input  wb,
  input  dest,
  input  rval,
  input  [2:0] func,
  output [3:0] src1_2,
  output [3:0] src2_2,
  output [3:0] dest_reg,
  output [7:0] output_2,
  output WR,
  output dest_2,
  output R_val,
  output [2:0] func_2
);

  Register #(.width(4)) register_1 (.D(src1), .Q(src1_2), .clk(clk));  // open: en, clr
  Register register_2 (.D(\output ), .Q(output_2), .clk(clk));  // open: en, clr
  Register #(.width(1)) register_3 (.D(wb), .Q(WR), .clk(clk));  // open: en, clr
  Register #(.width(1)) register_4 (.D(dest), .Q(dest_2), .clk(clk));  // open: en, clr
  Register #(.width(1)) register_5 (.D(rval), .Q(R_val), .clk(clk));  // open: en, clr
  Register #(.width(3)) register_6 (.D(func), .Q(func_2), .clk(clk));  // open: en, clr
  Register #(.width(4)) register_7 (.D(src2), .Q(src2_2), .clk(clk));  // open: en, clr
  Register #(.width(4)) register_8 (.D(des_reg), .Q(dest_reg), .clk(clk));  // open: en, clr
endmodule
